// Logisim project cpu-harness.circ as structural Verilog: 1 circuit, main circuit main
module main (
  output [15:0] r0,
  output [15:0] r1,
  output [15:0] r2,
  output [15:0] r3,
  output [15:0] d0,
  output [15:0] d1,
  output [15:0] Clock_Count,
  output [15:0] Data_Mem_Data,
  output [15:0] Data_Mem_Addr,
  output Write_Enabled
);

  wire clock_1_out;
  wire [15:0] adder_1_out, main_1_data_mem_addr, main_1_data_mem_data, main_1_to_instr_mem, rom_1_data;

  ROM #(.addrWidth(16), .dataWidth(16)) rom_1 (.addr(main_1_to_instr_mem), .data(rom_1_data));  // open: sel
  cpu_main main_1 (
    .To_Instr_Mem(main_1_to_instr_mem), .From_Instr_Mem(rom_1_data), .Data_Mem_Data(main_1_data_mem_data),
    .Data_Mem_Addr(main_1_data_mem_addr), .Data_Mem_Write(Write_Enabled), .r0(r0), .r1(r1), .r2(r2), .r3(r3),
    .Display_0(d0), .Display_1(d1), .clk(clock_1_out));
  Multiplexer #(.width(16), .enable("false")) multiplexer_1 (
    .in0({16{1'b0}}), .in1(main_1_data_mem_data), .out(Data_Mem_Data), .sel(Write_Enabled));
  Multiplexer #(.width(16), .enable("false")) multiplexer_2 (
    .in0({16{1'b0}}), .in1(main_1_data_mem_addr), .out(Data_Mem_Addr), .sel(Write_Enabled));
  Clock clock_1 (.out(clock_1_out));
  Register #(.width(16)) register_1 (.D(adder_1_out), .Q(Clock_Count), .clk(clock_1_out));  // open: en, clr
  Adder #(.width(16)) adder_1 (.a(16'h1), .b(Clock_Count), .out(adder_1_out));  // open: cin, cout

  // Notes on the sheet:
  //   contents of rom_1 (hex, n*v repeats v):
  //   5500 b600 5f00 4f08 b84 b701 b80 b702 5000 9703 208 4501 7009 5500 5f00 4f08 385 c603 52ff c604 2133
  //   3544 2233 3a44 96ff
endmodule
