// Logisim project cpu.circ as structural Verilog: 9 circuits, main circuit main
module main (
  input  [15:0] From_Instr_Mem,
  input  clk,
  output [15:0] r0,
  output [15:0] r1,
  output [15:0] r2,
  output [15:0] r3,
  output [15:0] Display_0,
  output [15:0] Display_1,
  output [15:0] Data_Mem_Data,
  output [15:0] To_Instr_Mem,
  output [15:0] Data_Mem_Addr,
  output Data_Mem_Write
);

  wire ALU_signed_overflow, ALUSrc, Br, Branch, DISP, equal, ExOp, J, JAL, JR, Jump, LUI, MemRead, MemToReg,
       not_1_out, or_1_out, or_2_out, RegDst, RegWrite;
  wire [1:0] WRITEREG_writereg;
  wire [2:0] ALUOp;
  wire [3:0] ALU_CONTROL_aluswitch;
  wire [5:0] funct;
  wire [7:6] imm;
  wire [15:0] ADD_2_out_3, ADD_out_3, alu_inputs_1_input_1, alu_inputs_1_input_2, controlled_buffer_1_out,
       demultiplexer_1_out0, demultiplexer_1_out1, imm_addr, JUMP_nextpc, multiplexer_1_out,
       multiplexer_2_out, multiplexer_3_out, multiplexer_4_out, multiplexer_5_out, rsAddr_rs, wdfr;
  wire [15:8] instr;

  Register #(.width(16)) register_1 (.D(multiplexer_4_out), .en(1'b1), .Q(To_Instr_Mem), .clk(clk));  // open: clr
  or or_1 (or_1_out, Jump, Branch);
  JUMP_TYPE JUMP_TYPE (.Jump(Jump), .RegWrite(RegWrite), .OpCode(instr[15:12]), .JAL(JAL), .J(J), .JR(JR));
  Comparator #(.width(4)) comparator_1 (.a(instr[15:12]), .b(4'b0010), .eq(LUI));  // open: gt, lt
  Comparator #(.width(4)) comparator_2 (.a(instr[15:12]), .b(4'b0001), .eq(DISP));  // open: gt, lt
  ADD ADD (.in_1(To_Instr_Mem), .in_2(16'h1), .out_3(ADD_out_3));  // open: Signed_Overflow
  Multiplexer #(.width(16), .enable("false")) multiplexer_1 (
    .in0(From_Instr_Mem), .in1({16{1'b0}}), .out(multiplexer_1_out), .sel(or_1_out));
  Register #(.width(16)) register_2 (.D(multiplexer_1_out), .Q({instr, imm, funct}), .clk(clk));  // open: en, clr
  BRANCH u_BRANCH (.br(Br), .equal(equal), .OpCode(instr[15:12]), .branch(Branch));
  JUMP u_JUMP (.PC(To_Instr_Mem), .instr_11_0({instr[11:8], imm, funct}), .nextPC(JUMP_nextpc));
  ADD ADD_2 (.in_1(To_Instr_Mem), .in_2(imm_addr), .out_3(ADD_2_out_3));  // open: Signed_Overflow
  CONTROL CONTROL (
    .opcode(instr[15:12]), .RegDst(RegDst), .Jump(Jump), .Branch(Br), .MemRead(MemRead), .MemtoReg(MemToReg),
    .ALUOp(ALUOp), .MemWrite(Data_Mem_Write), .ALUSrc(ALUSrc), .RegWrite(RegWrite), .ExOp(ExOp));
  WRITE_REG WRITEREG (.rt(instr[9:8]), .rd(imm), .RegDst(RegDst), .JAL(JAL), .WriteReg(WRITEREG_writereg));
  Multiplexer #(.width(16)) multiplexer_2 (
    .in0(ADD_out_3), .in1(ADD_2_out_3), .out(multiplexer_2_out), .sel(Branch));  // open: en
  SIGN_EXTEND sign_extend_1 (.imm({imm, funct}), .ExOp(ExOp), .out_3(imm_addr));
  Multiplexer #(.width(16)) multiplexer_3 (
    .in0(multiplexer_2_out), .in1(JUMP_nextpc), .out(multiplexer_3_out), .sel(Jump));  // open: en
  Regfile_main RegFile (
    .Read_register_1(instr[11:10]), .Read_register_2(instr[9:8]), .write_register(WRITEREG_writereg),
    .write_data(Data_Mem_Data), .Reg_0_Value(r0), .Reg_1_Value(r1), .Reg_2_Value(r2), .Reg_3_Value(r3),
    .RegWrite(RegWrite), .clock(clk), .Read_Data_1(rsAddr_rs), .Read_Data_2(wdfr));
  ALU_INPUTS alu_inputs_1 (
    .rs(rsAddr_rs), .rt(wdfr), .imm(imm_addr), .ALUSrc(ALUSrc), .Br(Br), .LUI(LUI),
    .INPUT_1(alu_inputs_1_input_1), .INPUT_2(alu_inputs_1_input_2));
  ALUControl ALU_CONTROL (.funct(funct), .ALUOp(ALUOp), .ALUSwitch(ALU_CONTROL_aluswitch));
  Multiplexer #(.width(16)) multiplexer_4 (
    .in0(multiplexer_3_out), .in1(rsAddr_rs), .out(multiplexer_4_out), .sel(JR));  // open: en
  LED Signed_Oveflow (.in(ALU_signed_overflow));
  alu_main ALU (
    .switch__S(ALU_CONTROL_aluswitch), .X(alu_inputs_1_input_1), .equal(equal), .result(Data_Mem_Addr),
    .signed_overflow(ALU_signed_overflow), .Y(alu_inputs_1_input_2));
  // BlockTop blocktop_1: pin names not known; wires that end beside it: alu_inputs_1_input_1, alu_inputs_1_input_2
  // _7_Segment_Display 7_segment_display_1: pin names not known; wires that end beside it: Display_0[15:12], Display_0[15:12]
  // _7_Segment_Display 7_segment_display_2: pin names not known; wires that end beside it: Display_0[15:12], Display_0[15:12], Display_0[11:8], Display_0[11:8], Display_0[7:4], Display_0[7:4], Display_0[3:0], Display_0[3:0]
  // BlockBottom blockbottom_1: pin names not known
  not not_1 (not_1_out, Data_Mem_Write);
  // _7_Segment_Display 7_segment_display_3: pin names not known; wires that end beside it: Display_0[15:12], Display_0[15:12], Display_0[11:8], Display_0[11:8], Display_0[7:4], Display_0[7:4], Display_0[3:0], Display_0[3:0]
  // _7_Segment_Display 7_segment_display_4: pin names not known; wires that end beside it: Display_0[3:0], Display_0[3:0]
  Demultiplexer #(.width(16), .tristate("true")) demultiplexer_1 (
    .out0(demultiplexer_1_out0), .out1(demultiplexer_1_out1), .in(rsAddr_rs), .sel(imm_addr[0]), .en(DISP));
  assign controlled_buffer_1_out = Data_Mem_Write ? wdfr : 16'bz;  // Controlled_Buffer controlled_buffer_1
  RAM #(.addrWidth(16), .dataWidth(16)) ram_1 (
    .addr(Data_Mem_Addr), .data(controlled_buffer_1_out), .sel(1'b1), .clk(clk), .ld(not_1_out), .clr(1'b0));
  // _7_Segment_Display 7_segment_display_5: pin names not known; wires that end beside it: Display_1[15:12], Display_1[15:12]
  // BlockBottom blockbottom_2: pin names not known
  or or_2 (or_2_out, Data_Mem_Write, MemToReg);
  // BlockTop blocktop_2: pin names not known
  // _7_Segment_Display 7_segment_display_6: pin names not known; wires that end beside it: Display_1[15:12], Display_1[15:12], Display_1[11:8], Display_1[11:8], Display_1[7:4], Display_1[7:4], Display_1[3:0], Display_1[3:0]
  // _7_Segment_Display 7_segment_display_7: pin names not known; wires that end beside it: Display_1[15:12], Display_1[15:12], Display_1[11:8], Display_1[11:8], Display_1[7:4], Display_1[7:4], Display_1[3:0], Display_1[3:0]
  Register #(.width(16)) register_3 (.D(demultiplexer_1_out0), .Q(Display_0), .clk(clk));  // open: en, clr
  Register #(.width(16)) register_4 (.D(demultiplexer_1_out1), .Q(Display_1), .clk(clk));  // open: en, clr
  Multiplexer #(.width(16)) multiplexer_5 (
    .in0(Data_Mem_Addr), .in1(controlled_buffer_1_out), .out(multiplexer_5_out), .sel(or_2_out));  // open: en
  Multiplexer #(.width(16)) multiplexer_6 (
    .in0(multiplexer_5_out), .in1(To_Instr_Mem), .out(Data_Mem_Data), .sel(JAL));  // open: en
  // _7_Segment_Display 7_segment_display_8: pin names not known; wires that end beside it: Display_1[3:0], Display_1[3:0]

  // Other names for the same wires on the sheet: d0[15:0] = Display_0; d1[15:0] = Display_1; imm[5:0] = funct;
  //   instr[7:0] = {imm, funct}; rd[1:0] = imm; rt[1:0] = instr[9:8]; rs[1:0] = instr[11:10];
  //   OpCode[3:0] = instr[15:12]; MemWrite = Data_Mem_Write; PC[15:0] = To_Instr_Mem; result[15:0] = Data_Mem_Addr;
  //   wd[15:0] = Data_Mem_Data

  // Notes on the sheet:
  //   DISPLAY[0]
  //   BlockTop
  //   BlockBottom
  //   DISPLAY[0]
  //   BlockTop
  //   BlockBottom
endmodule

module CONTROL (
  input  [3:0] opcode,
  output RegDst,
  output Jump,
  output Branch,
  output MemRead,
  output MemtoReg,
  output [2:0] ALUOp,
  output MemWrite,
  output ALUSrc,
  output RegWrite,
  output ExOp
);

  Multiplexer #(.select(4), .width(12), .enable("false")) multiplexer_1 (
    .in0(12'h802), .in1(12'h76), .in2(12'h16), .in3(12'h26), .in4(12'h37), .in5(12'h46), .in6(12'h472),
    .in7(12'h470), .in8(12'h470), .in9(12'h275), .in10(12'h275), .in11(12'h1b7), .in12(12'h3d),
    .out({RegDst, Jump, Branch, MemRead, MemtoReg, ALUOp, MemWrite, ALUSrc, RegWrite, ExOp}), .sel(opcode));  // open: in13, in14, in15
endmodule

module ALUControl (
  input  [5:0] funct,
  input  [2:0] ALUOp,
  output [3:0] ALUSwitch
);

  Multiplexer #(.select(3), .width(4), .enable("false")) multiplexer_1 (
    .in0(funct[3:0]), .in1(4'b0100), .in2(4'b0000), .in3(4'b0010), .in4(4'b0001), .in5(4'b1111),
    .in6(4'b1111), .in7(4'b1111), .out(ALUSwitch), .sel(ALUOp));
endmodule

module BRANCH (
  input  br,
  input  equal,
  input  [3:0] OpCode,
  output branch
);

  wire and_1_out, and_2_out, not_1_out, not_2_out;

  not not_1 (not_1_out, equal);
  not not_2 (not_2_out, OpCode[0]);
  and and_1 (and_1_out, br, equal, OpCode[0]);
  and and_2 (and_2_out, br, not_1_out, not_2_out);
  or or_1 (branch, and_1_out, and_2_out);
endmodule

module SIGN_EXTEND (
  input  [7:0] imm,
  input  ExOp,
  output [15:0] out_3
);

  wire [15:0] bit_extender_1_out, bit_extender_2_out;

  assign bit_extender_1_out = {{8{1'b0}}, imm};  // Bit_Extender bit_extender_1
  assign bit_extender_2_out = {{8{imm[7]}}, imm};  // Bit_Extender bit_extender_2
  Multiplexer #(.width(16)) multiplexer_1 (
    .in0(bit_extender_1_out), .in1(bit_extender_2_out), .out(out_3), .sel(ExOp));  // open: en
endmodule

module JUMP (
  input  [15:0] PC,
  input  [11:0] instr_11_0,
  output [15:0] nextPC
);

  wire [15:0] and_1_out, bit_extender_1_out;

  assign and_1_out = PC & 16'hf000;  // AND_Gate and_1, 16 bits wide
  assign bit_extender_1_out = {{4{1'b0}}, instr_11_0};  // Bit_Extender bit_extender_1
  assign nextPC = and_1_out | bit_extender_1_out;  // OR_Gate or_1, 16 bits wide
endmodule

module JUMP_TYPE (
  input  Jump,
  input  RegWrite,
  input  [3:0] OpCode,
  output JAL,
  output J,
  output JR
);

  wire not_1_out, not_2_out, not_3_out;

  not not_1 (not_1_out, RegWrite);
  not not_2 (not_2_out, OpCode[0]);
  and and_1 (JAL, Jump, not_2_out, RegWrite);
  not not_3 (not_3_out, OpCode[0]);
  and and_2 (J, Jump, not_1_out, OpCode[0]);
  and and_3 (JR, Jump, not_1_out, not_3_out);
endmodule

module WRITE_REG (
  input  [1:0] rt,
  input  [1:0] rd,
  input  RegDst,
  input  JAL,
  output [1:0] WriteReg
);

  wire [1:0] multiplexer_1_out;

  Multiplexer #(.width(2)) multiplexer_1 (.in0(rt), .in1(rd), .out(multiplexer_1_out), .sel(RegDst));  // open: en
  Multiplexer #(.width(2)) multiplexer_2 (.in0(multiplexer_1_out), .in1(2'b11), .out(WriteReg), .sel(JAL));  // open: en
endmodule

module ALU_INPUTS (
  input  [15:0] rs,
  input  [15:0] rt,
  input  [15:0] imm,
  input  ALUSrc,
  input  Br,
  input  LUI,
  output [15:0] INPUT_1,
  output [15:0] INPUT_2
);

  wire and_1_out, not_1_out;
  wire [15:0] multiplexer_1_out;

  and and_1 (and_1_out, ALUSrc, not_1_out);
  Multiplexer #(.width(16)) multiplexer_1 (.in0(rt), .in1(imm), .out(multiplexer_1_out), .sel(and_1_out));  // open: en
  not not_1 (not_1_out, Br);
  Multiplexer #(.width(16)) multiplexer_2 (.in0(multiplexer_1_out), .in1(16'h8), .out(INPUT_2), .sel(LUI));  // open: en
  Multiplexer #(.width(16)) multiplexer_3 (.in0(rs), .in1(imm), .out(INPUT_1), .sel(LUI));  // open: en
endmodule
