// Logisim project Regfile.circ as structural Verilog: 2 circuits, main circuit main
module main (
  input  [1:0] Read_register_1,
  input  [1:0] Read_register_2,
  input  [1:0] write_register,
  input  [15:0] write_data,
  input  RegWrite,
  input  clock,
  output [15:0] Reg_0_Value,
  output [15:0] Reg_1_Value,
  output [15:0] Reg_2_Value,
  output [15:0] Reg_3_Value,
  output [15:0] Read_Data_1,
  output [15:0] Read_Data_2
);

  WRITE write_1 (
    .write_register(write_register), .write_data(write_data), .RegWrite(RegWrite), .clock(clock),
    .Reg_0_Value(Reg_0_Value), .Reg_1_Value(Reg_1_Value), .Reg_2_Value(Reg_2_Value), .Reg_3_Value(Reg_3_Value));
  Multiplexer #(.select(2), .width(16)) multiplexer_1 (
    .in0(Reg_0_Value), .in1(Reg_1_Value), .in2(Reg_2_Value), .in3(Reg_3_Value), .out(Read_Data_1),
    .sel(Read_register_1));  // open: en
  Multiplexer #(.select(2), .width(16)) multiplexer_2 (
    .in0(Reg_0_Value), .in1(Reg_1_Value), .in2(Reg_2_Value), .in3(Reg_3_Value), .out(Read_Data_2),
    .sel(Read_register_2));  // open: en

  // Notes on the sheet:
  //   WRITE
endmodule

module WRITE (
  input  [1:0] write_register,
  input  [15:0] write_data,
  input  RegWrite,
  input  clock,
  output [15:0] Reg_0_Value,
  output [15:0] Reg_1_Value,
  output [15:0] Reg_2_Value,
  output [15:0] Reg_3_Value
);

  wire [15:0] demultiplexer_1_out0, demultiplexer_1_out1, demultiplexer_1_out2, demultiplexer_1_out3,
       multiplexer_1_out;

  Multiplexer #(.width(16)) multiplexer_1 (.in1(write_data), .out(multiplexer_1_out), .sel(RegWrite));  // open: in0, en
  Demultiplexer #(.select(2), .width(16), .tristate("true")) demultiplexer_1 (
    .out0(demultiplexer_1_out0), .out1(demultiplexer_1_out1), .out2(demultiplexer_1_out2),
    .out3(demultiplexer_1_out3), .in(multiplexer_1_out), .sel(write_register));  // open: en
  Register #(.width(16)) register_1 (.D(demultiplexer_1_out0), .Q(Reg_0_Value), .clk(clock));  // open: en, clr
  Register #(.width(16)) register_2 (.D(demultiplexer_1_out1), .Q(Reg_1_Value), .clk(clock));  // open: en, clr
  Register #(.width(16)) register_3 (.D(demultiplexer_1_out2), .Q(Reg_2_Value), .clk(clock));  // open: en, clr
  Register #(.width(16)) register_4 (.D(demultiplexer_1_out3), .Q(Reg_3_Value), .clk(clock));  // open: en, clr
endmodule
