// Logisim project alu.circ as structural Verilog: 8 circuits, main circuit main
module main (
  input  [15:0] X,
  input  [15:0] Y,
  input  [3:0] switch__S,
  output signed_overflow,
  output [15:0] result,
  output equal
);

  wire add_1_signed_overflow, addp8_1_out_4, sub_1_out_4, subp8_1_signed_overflow;
  wire [0:0] comparator_1_lt;
  wire [15:0] add_1_out_3, addp8_1_out_3, and_1_out, or_1_out, shifter_1_out, shifter_2_out, shifter_3_out,
       sltp8_1_out_3, sub_1_out_3, subp8_1_out_3;

  ADD add_1 (.in_1(X), .in_2(Y), .out_3(add_1_out_3), .Signed_Overflow(add_1_signed_overflow));
  SUB sub_1 (.in_1(X), .in_2(Y), .out_3(sub_1_out_3), .out_4(sub_1_out_4));
  assign or_1_out = X | Y;  // OR_Gate or_1, 16 bits wide
  assign and_1_out = X & Y;  // AND_Gate and_1, 16 bits wide
  Shifter #(.width(16)) shifter_1 (.in(X), .\dist (Y[3:0]), .out(shifter_1_out));
  Shifter #(.width(16), .shift("lr")) shifter_2 (.in(X), .\dist (Y[3:0]), .out(shifter_2_out));
  Shifter #(.width(16), .shift("ar")) shifter_3 (.in(X), .\dist (Y[3:0]), .out(shifter_3_out));
  Comparator #(.width(16)) comparator_1 (.a(X), .b(Y), .lt(comparator_1_lt[0]));  // open: gt, eq
  ADDP8 addp8_1 (.in_1(X), .in_2(Y), .out_3(addp8_1_out_3), .out_4(addp8_1_out_4));
  SUBP8 subp8_1 (.in_1(X), .in_2(Y), .out_3(subp8_1_out_3), .Signed_Overflow(subp8_1_signed_overflow));
  SLTP8 sltp8_1 (.in_1(X), .in_2(Y), .out_3(sltp8_1_out_3));
  Comparator #(.width(16)) comparator_2 (.a(X), .b(Y), .eq(equal));  // open: gt, lt
  Multiplexer #(.select(4)) multiplexer_1 (
    .in0(1'b0), .in1(1'b0), .in2(add_1_signed_overflow), .in3(sub_1_out_4), .in4(1'b0), .in5(1'b0),
    .in6(1'b0), .in7(1'b0), .in8(addp8_1_out_4), .in9(subp8_1_signed_overflow), .in10(1'b0), .in11(1'b0),
    .in12(1'b0), .in13(1'b0), .in14(1'b0), .in15(1'b0), .out(signed_overflow), .sel(switch__S));  // open: en
  Multiplexer #(.select(4), .width(16)) multiplexer_2 (
    .in0(or_1_out), .in1(and_1_out), .in2(add_1_out_3), .in3(sub_1_out_3), .in4(shifter_1_out),
    .in5(shifter_2_out), .in6(shifter_3_out), .in7({{15{1'b0}}, comparator_1_lt[0]}), .in8(addp8_1_out_3),
    .in9(subp8_1_out_3), .in10(sltp8_1_out_3), .in11({16{1'b0}}), .in12({16{1'b0}}), .in13({16{1'b0}}),
    .in14({16{1'b0}}), .in15({16{1'b0}}), .out(result), .sel(switch__S));  // open: en

  // Notes on the sheet:
  //   OR=0000
  //   AND=0001
  //   ADD=0010
  //   SUB=0011
  //   SLLV=0100
  //   SRLV=0101
  //   SRAV=0110
  //   SLT=0111
  //   ADDP8=1000
  //   SUBP8=1001
  //   SLTP8=1010
endmodule

module ADD (
  input  [15:0] in_1,
  input  [15:0] in_2,
  output [15:0] out_3,
  output Signed_Overflow
);

  wire and_1_out, and_2_out, not_1_out, not_2_out, not_3_out;

  Adder #(.width(16)) adder_1 (.a(in_1), .b(in_2), .out(out_3));  // open: cin, cout
  not not_1 (not_1_out, out_3[15]);
  not not_2 (not_2_out, in_1[15]);
  not not_3 (not_3_out, in_2[15]);
  and and_1 (and_1_out, in_1[15], not_1_out, in_2[15]);
  and and_2 (and_2_out, not_2_out, out_3[15], not_3_out);
  or or_1 (Signed_Overflow, and_1_out, and_2_out);
endmodule

module SUB (
  input  [15:0] in_1,
  input  [15:0] in_2,
  output [15:0] out_3,
  output out_4
);

  wire and_1_out, and_2_out, not_1_out, not_2_out, not_3_out;

  Subtractor #(.width(16)) subtractor_1 (.a(in_1), .b(in_2), .out(out_3));  // open: bin, bout
  not not_1 (not_1_out, out_3[15]);
  not not_2 (not_2_out, in_2[15]);
  not not_3 (not_3_out, in_1[15]);
  and and_1 (and_1_out, in_1[15], not_1_out, not_2_out);
  and and_2 (and_2_out, not_3_out, out_3[15], in_2[15]);
  or or_1 (out_4, and_1_out, and_2_out);

  // Notes on the sheet:
  //   Signed Overflow
endmodule

module ADD8 (
  input  [7:0] in_1,
  input  [7:0] in_2,
  output [7:0] out_3,
  output Signed_Overflow
);

  wire and_1_out, and_2_out, not_1_out, not_2_out, not_3_out;

  Adder adder_1 (.a(in_1), .b(in_2), .out(out_3));  // open: cin, cout
  not not_1 (not_1_out, out_3[7]);
  not not_2 (not_2_out, in_1[7]);
  not not_3 (not_3_out, in_2[7]);
  and and_1 (and_1_out, in_1[7], not_1_out, in_2[7]);
  and and_2 (and_2_out, not_2_out, out_3[7], not_3_out);
  or or_1 (Signed_Overflow, and_1_out, and_2_out);
endmodule

module ADDP8 (
  input  [15:0] in_1,
  input  [15:0] in_2,
  output [15:0] out_3,
  output out_4
);

  wire add8_1_signed_overflow, add8_2_signed_overflow;

  ADD8 add8_1 (.in_1(in_1[7:0]), .in_2(in_2[7:0]), .out_3(out_3[7:0]), .Signed_Overflow(add8_1_signed_overflow));
  ADD8 add8_2 (.in_1(in_1[15:8]), .in_2(in_2[15:8]), .out_3(out_3[15:8]), .Signed_Overflow(add8_2_signed_overflow));
  or or_1 (out_4, add8_1_signed_overflow, add8_2_signed_overflow);

  // Notes on the sheet:
  //   A
  //   B
  //   ADD8
  //   ADD8
  //   Signed Overflow
endmodule

module SUB8 (
  input  [7:0] in_1,
  input  [7:0] in_2,
  output [7:0] out_3,
  output out_4
);

  wire and_1_out, and_2_out, not_1_out, not_2_out, not_3_out;

  Subtractor subtractor_1 (.a(in_1), .b(in_2), .out(out_3));  // open: bin, bout
  not not_1 (not_1_out, out_3[7]);
  not not_2 (not_2_out, in_2[7]);
  not not_3 (not_3_out, in_1[7]);
  and and_1 (and_1_out, in_1[7], not_1_out, not_2_out);
  and and_2 (and_2_out, not_3_out, out_3[7], in_2[7]);
  or or_1 (out_4, and_1_out, and_2_out);

  // Notes on the sheet:
  //   Signed Overflow
endmodule

module SUBP8 (
  input  [15:0] in_1,
  input  [15:0] in_2,
  output [15:0] out_3,
  output Signed_Overflow
);

  wire sub8_1_out_4, sub8_2_out_4;

  SUB8 sub8_1 (.in_1(in_1[7:0]), .in_2(in_2[7:0]), .out_3(out_3[7:0]), .out_4(sub8_1_out_4));
  SUB8 sub8_2 (.in_1(in_1[15:8]), .in_2(in_2[15:8]), .out_3(out_3[15:8]), .out_4(sub8_2_out_4));
  or or_1 (Signed_Overflow, sub8_1_out_4, sub8_2_out_4);

  // Notes on the sheet:
  //   SUB8
  //   SUB8
endmodule

module SLTP8 (
  input  [15:0] in_1,
  input  [15:0] in_2,
  output [15:0] out_3
);

  Comparator comparator_1 (.a(in_1[7:0]), .b(in_2[7:0]), .lt(out_3[0]));  // open: gt, eq
  Comparator comparator_2 (.a(in_1[15:8]), .b(in_2[15:8]), .lt(out_3[8]));  // open: gt, eq

  assign {out_3[15:9], out_3[7:1]} = {14{1'b0}};
endmodule
